// Logisim project EXERCISE1----604-2017.circ as structural Verilog: 2 circuits, main circuit main
module main (
  input  A,
  input  B,
  input  C,
  output F
);

  wire U1_out, U2_out;

  not U1 (U1_out, A);
  and U2 (U2_out, U1_out, B);
  or U3 (F, U2_out, C);
endmodule

module Verification (
  input  A,
  input  B,
  input  C,
  output F
);

  wire and_1_out, not_1_out;

  not not_1 (not_1_out, A);
  and and_1 (and_1_out, not_1_out, B);
  or or_1 (F, and_1_out, C);
endmodule
