// Logisim project EXERCISE2-logism---604-2017.circ as structural Verilog: 8 circuits, main circuit main
module main (
  input  A,
  input  B,
  input  C,
  input  D
);

  wire fa_1_fa, fb_1_fb, fc_1_fc, fd_1_fd, fe_1_fe, ff_1_ff, fg_1_fg;

  Fa fa_1 (.A(A), .B(B), .C(C), .D(D), .Fa(fa_1_fa));
  Fb fb_1 (.A(A), .B(B), .C(C), .D(D), .Fb(fb_1_fb));
  Fc fc_1 (.A(A), .B(B), .C(C), .D(D), .Fc(fc_1_fc));
  Fd fd_1 (.A(A), .B(B), .C(C), .D(D), .Fd(fd_1_fd));
  Fe fe_1 (.A(A), .B(B), .C(C), .D(D), .Fe(fe_1_fe));
  Ff ff_1 (.A(A), .B(B), .C(C), .D(D), .Ff(ff_1_ff));
  Fg fg_1 (.A(A), .B(B), .C(C), .D(D), .Fg(fg_1_fg));
  _7_Segment_Display #(.active("false")) u_7_segment_display_1 (
    .g(fg_1_fg), .f(ff_1_ff), .a(fa_1_fa), .b(fb_1_fb), .e(fe_1_fe), .d(fd_1_fd), .c(fc_1_fc), .dp(1'b1));
endmodule

module Fa (
  input  A,
  input  B,
  input  C,
  input  D,
  output Fa
);

  wire and_1_out, and_2_out, and_3_out, and_4_out, not_1_out, not_2_out, not_3_out, not_4_out, not_5_out,
       not_6_out;

  not not_1 (not_1_out, A);
  not not_2 (not_2_out, B);
  not not_3 (not_3_out, C);
  not not_4 (not_4_out, D);
  not not_5 (not_5_out, B);
  not not_6 (not_6_out, C);
  and and_1 (and_1_out, not_1_out, not_2_out, not_3_out, D);
  and and_2 (and_2_out, not_1_out, B, not_3_out, not_4_out);
  and and_3 (and_3_out, A, not_5_out, C, D);
  and and_4 (and_4_out, A, B, not_6_out, D);
  or or_1 (Fa, and_1_out, and_2_out, and_3_out, and_4_out);
endmodule

module Fb (
  input  A,
  input  B,
  input  C,
  input  D,
  output Fb
);

  wire and_1_out, and_2_out, and_3_out, and_4_out, and_5_out, not_1_out, not_2_out, not_3_out, not_4_out;

  not not_1 (not_1_out, D);
  not not_2 (not_2_out, D);
  not not_3 (not_3_out, A);
  not not_4 (not_4_out, C);
  and and_1 (and_1_out, B, C, not_1_out);
  and and_2 (and_2_out, A, B, C);
  and and_3 (and_3_out, A, C, D);
  and and_4 (and_4_out, A, B, not_2_out);
  and and_5 (and_5_out, not_3_out, B, not_4_out, D);
  or or_1 (Fb, and_1_out, and_2_out, and_3_out, and_4_out, and_5_out);
endmodule

module Fc (
  input  A,
  input  B,
  input  C,
  input  D,
  output Fc
);

  wire and_1_out, and_2_out, and_3_out, not_1_out, not_2_out, not_3_out, not_4_out;

  not not_1 (not_1_out, D);
  not not_2 (not_2_out, A);
  not not_3 (not_3_out, B);
  not not_4 (not_4_out, D);
  and and_1 (and_1_out, A, B, C);
  and and_2 (and_2_out, A, B, not_1_out);
  and and_3 (and_3_out, not_2_out, not_3_out, C, not_4_out);
  or or_1 (Fc, and_1_out, and_2_out, and_3_out);
endmodule

module Fd (
  input  A,
  input  B,
  input  C,
  input  D,
  output Fd
);

  wire and_1_out, and_2_out, and_3_out, and_4_out, not_1_out, not_2_out, not_3_out, not_4_out;

  not not_1 (not_1_out, A);
  not not_2 (not_2_out, B);
  not not_3 (not_3_out, C);
  not not_4 (not_4_out, D);
  and and_1 (and_1_out, B, C, D);
  and and_2 (and_2_out, not_1_out, not_2_out, not_3_out, D);
  and and_3 (and_3_out, not_1_out, B, not_3_out, not_4_out);
  and and_4 (and_4_out, A, not_2_out, C, not_4_out);
  or or_1 (Fd, and_1_out, and_2_out, and_3_out, and_4_out);
endmodule

module Fe (
  input  A,
  input  B,
  input  C,
  input  D,
  output Fe
);

  wire and_1_out, and_2_out, and_3_out, not_1_out, not_2_out, not_3_out;

  not not_1 (not_1_out, A);
  not not_2 (not_2_out, C);
  not not_3 (not_3_out, B);
  and and_1 (and_1_out, not_1_out, D);
  and and_2 (and_2_out, not_1_out, B, not_2_out);
  and and_3 (and_3_out, not_3_out, not_2_out, D);
  or or_1 (Fe, and_1_out, and_2_out, and_3_out);
endmodule

module Ff (
  input  A,
  input  B,
  input  C,
  input  D,
  output Ff
);

  wire and_1_out, and_2_out, and_3_out, and_4_out, not_1_out, not_2_out, not_3_out;

  not not_1 (not_1_out, A);
  not not_2 (not_2_out, B);
  not not_3 (not_3_out, C);
  and and_1 (and_1_out, not_1_out, not_2_out, D);
  and and_2 (and_2_out, not_1_out, not_2_out, C);
  and and_3 (and_3_out, not_1_out, C, D);
  and and_4 (and_4_out, A, B, not_3_out, D);
  or or_1 (Ff, and_1_out, and_2_out, and_3_out, and_4_out);
endmodule

module Fg (
  input  A,
  input  B,
  input  C,
  input  D,
  output Fg
);

  wire and_1_out, and_2_out, and_3_out, not_1_out, not_2_out, not_3_out, not_4_out;

  not not_1 (not_1_out, A);
  not not_2 (not_2_out, B);
  not not_3 (not_3_out, C);
  not not_4 (not_4_out, D);
  and and_1 (and_1_out, not_1_out, not_2_out, not_3_out);
  and and_2 (and_2_out, not_1_out, B, C, D);
  and and_3 (and_3_out, A, B, not_3_out, not_4_out);
  or or_1 (Fg, and_1_out, and_2_out, and_3_out);
endmodule
