// Logisim project 8 bit-alu-start.circ as structural Verilog: 1 circuit, main circuit main
module main (
  input  [7:0] in_1,
  input  [7:0] in_2,
  input  [1:0] in_3,
  output [7:0] out_4,
  output [7:0] out_5
);

  wire adder_1_cout, subtractor_1_bout;
  wire [3:0] bitselector_2_out, multiplexer_1_out;
  wire [7:0] adder_1_out, bitselector_1_out, divider_1_out, divider_1_rem, multiplier_1_cout,
       multiplier_1_out, subtractor_1_out;

  Hex_Digit_Display hex_digit_display_1 (.value(in_1[7:4]));  // open: dp
  Hex_Digit_Display hex_digit_display_2 (.value(in_1[3:0]));  // open: dp
  Hex_Digit_Display hex_digit_display_3 (.value(in_2[3:0]));  // open: dp
  Hex_Digit_Display hex_digit_display_4 (.value(in_2[7:4]));  // open: dp
  Adder adder_1 (.a(in_1), .b(in_2), .out(adder_1_out), .cin(1'b0), .cout(adder_1_cout));
  Subtractor subtractor_1 (.a(in_1), .b(in_2), .out(subtractor_1_out), .bin(1'b0), .bout(subtractor_1_bout));
  Multiplier multiplier_1 (.a(in_1), .b(in_2), .out(multiplier_1_out), .cin({8{1'b0}}), .cout(multiplier_1_cout));
  Divider divider_1 (.a(in_1), .b(in_2), .out(divider_1_out), .upper({8{1'b0}}), .rem(divider_1_rem));
  BitSelector #(.width(1), .group(8)) bitselector_1 (.in(adder_1_cout), .out(bitselector_1_out), .sel(1'b0));
  BitSelector #(.width(1), .group(4)) bitselector_2 (.in(subtractor_1_bout), .out(bitselector_2_out), .sel(1'b0));
  Multiplexer #(.select(2), .width(4), .enable("false")) multiplexer_1 (
    .in0(4'b0000), .in1(bitselector_2_out), .in2(4'b0000), .in3(4'b0000), .out(multiplexer_1_out), .sel(in_3));
  Multiplexer #(.select(2), .width(8), .enable("false")) multiplexer_2 (
    .in0(adder_1_out), .in1(subtractor_1_out), .in2(multiplier_1_out), .in3(divider_1_out), .out(out_5),
    .sel(in_3));
  Hex_Digit_Display hex_digit_display_5 (.value(multiplexer_1_out));  // open: dp
  Multiplexer #(.select(2), .width(8), .enable("false")) multiplexer_3 (
    .in0(bitselector_1_out), .in1({8{1'b0}}), .in2(multiplier_1_cout), .in3(divider_1_rem), .out(out_4),
    .sel(in_3));
  Hex_Digit_Display hex_digit_display_6 (.value(out_4[7:4]));  // open: dp
  Hex_Digit_Display hex_digit_display_7 (.value(out_4[3:0]));  // open: dp
  Hex_Digit_Display hex_digit_display_8 (.value(out_5[3:0]));  // open: dp
  Hex_Digit_Display hex_digit_display_9 (.value(out_5[7:4]));  // open: dp

  // Notes on the sheet:
  //   Πρόσημο
  //   Υπόλοιπο για διαίρεση
  //   Πηλίκο για διαίρεση
endmodule
