// Logisim project EXERCISE4----STATHAKOS---2017.circ as structural Verilog: 1 circuit, main circuit main
module main (
  input  X,
  output out_2
);

  wire _0_q, _0_qn, _1_q, _1_qn, _2_q, _2_qn, and_1_out, and_2_out, and_3_out, and_4_out, and_5_out,
       and_6_out, and_7_out, and_8_out, and_9_out, and_10_out, and_11_out, and_12_out, and_13_out,
       clock_1_out, not_1_out, not_2_out, not_3_out, not_4_out, or_1_out, or_2_out, or_3_out;

  not not_1 (not_1_out, X);
  not not_2 (not_2_out, X);
  not not_3 (not_3_out, X);
  not not_4 (not_4_out, X);
  and and_1 (and_1_out, X, _2_qn);
  and and_2 (and_2_out, _0_q, _1_q);
  and and_3 (and_3_out, X, _0_q);
  and and_4 (and_4_out, X, _1_q);
  and and_5 (and_5_out, not_2_out, _2_qn, _1_qn, _0_q);
  and and_6 (and_6_out, X, _1_qn, _2_q);
  and and_7 (and_7_out, _1_q, not_1_out, _2_q);
  and and_8 (and_8_out, X, _2_qn, _1_q, _0_qn);
  and and_9 (and_9_out, not_3_out, _2_qn, _1_q);
  and and_10 (and_10_out, not_4_out, _2_q, _0_q);
  and and_11 (and_11_out, _2_q, _1_qn, _0_qn, X);
  or or_1 (or_1_out, and_1_out, and_2_out, and_3_out, and_4_out);
  or or_2 (or_2_out, and_5_out, and_6_out, and_7_out, and_8_out);
  or or_3 (or_3_out, and_9_out, and_10_out, and_11_out);
  Clock clock_1 (.out(clock_1_out));
  D_Flip_Flop _0 (.clk(clock_1_out), .D(or_1_out), .Q(_0_q), .Qn(_0_qn));  // open: preset, en, reset
  D_Flip_Flop _1 (.clk(clock_1_out), .D(or_2_out), .Q(_1_q), .Qn(_1_qn));  // open: preset, en, reset
  D_Flip_Flop _2 (.clk(clock_1_out), .D(or_3_out), .Q(_2_q), .Qn(_2_qn));  // open: preset, en, reset
  and and_12 (and_12_out, _0_q, _2_q);
  and and_13 (and_13_out, _1_q, _2_q);
  or or_4 (out_2, and_12_out, and_13_out);
endmodule
