// Logisim project ECE02017.circ as structural Verilog: 2 circuits, main circuit main
module main (
  input  in_1,
  input  in_2
);

  wire clock_1_out, text_out_1_fa, text_out_1_fb, text_out_1_fc, text_out_1_fd, text_out_1_fe, text_out_1_ff,
       text_out_1_fg;
  wire [3:0] counter_1_q;

  Clock clock_1 (.out(clock_1_out));
  Counter #(.width(4), .max('h7)) counter_1 (
    .D(counter_1_q), .Q(counter_1_q), .clk(clock_1_out), .clr(in_2));  // open: load, count, carry
  TEXT_OUT text_out_1 (
    .L(in_1), .A(counter_1_q[2]), .B(counter_1_q[1]), .C(counter_1_q[0]), .Fa(text_out_1_fa),
    .Fb(text_out_1_fb), .Fc(text_out_1_fc), .Fd(text_out_1_fd), .Fe(text_out_1_fe), .Ff(text_out_1_ff),
    .Fg(text_out_1_fg));
  _7_Segment_Display #(.active("false")) u_7_segment_display_1 (
    .g(text_out_1_fg), .f(text_out_1_ff), .a(text_out_1_fa), .b(text_out_1_fb), .e(text_out_1_fe),
    .d(text_out_1_fd), .c(text_out_1_fc), .dp(1'b1));
endmodule

module TEXT_OUT (
  input  L,
  input  A,
  input  B,
  input  C,
  output Fa,
  output Fb,
  output Fc,
  output Fd,
  output Fe,
  output Ff,
  output Fg
);

  wire and_1_out, and_2_out, and_3_out, and_4_out, and_5_out, and_6_out, and_7_out, and_8_out, and_9_out,
       and_10_out, and_11_out, and_12_out, and_13_out, and_14_out, and_15_out, and_16_out, and_17_out,
       and_18_out, and_19_out, and_20_out, and_21_out, and_22_out, and_23_out, and_24_out, not_1_out,
       not_2_out, not_3_out, not_4_out, not_5_out, not_6_out, not_7_out, not_8_out, not_9_out, not_10_out,
       not_11_out, not_12_out, not_13_out, not_14_out, not_15_out, not_16_out, not_17_out, not_18_out,
       not_19_out, not_20_out, not_21_out, not_22_out, not_23_out, not_24_out, not_25_out, not_26_out,
       not_27_out, not_28_out, not_29_out, not_30_out, not_31_out, not_32_out, not_33_out, not_34_out,
       not_35_out, not_36_out;

  not not_1 (not_1_out, L);
  not not_2 (not_2_out, C);
  not not_3 (not_3_out, A);
  not not_4 (not_4_out, B);
  not not_5 (not_5_out, L);
  not not_6 (not_6_out, A);
  and and_1 (and_1_out, not_5_out, not_6_out, not_7_out);
  not not_7 (not_7_out, B);
  not not_8 (not_8_out, L);
  not not_9 (not_9_out, A);
  and and_2 (and_2_out, not_8_out, not_9_out, not_10_out);
  not not_10 (not_10_out, C);
  and and_3 (and_3_out, L, A, C);
  and and_4 (and_4_out, L, A, B);
  not not_11 (not_11_out, L);
  not not_12 (not_12_out, A);
  and and_5 (and_5_out, not_11_out, not_12_out, not_13_out);
  not not_13 (not_13_out, B);
  not not_14 (not_14_out, L);
  not not_15 (not_15_out, A);
  and and_6 (and_6_out, not_14_out, not_15_out, not_16_out);
  not not_16 (not_16_out, C);
  not not_17 (not_17_out, L);
  and and_7 (and_7_out, not_17_out, not_18_out, not_19_out);
  not not_18 (not_18_out, B);
  not not_19 (not_19_out, C);
  and and_8 (and_8_out, L, B, C);
  and and_9 (and_9_out, L, A, C);
  and and_10 (and_10_out, L, A, B);
  not not_20 (not_20_out, L);
  and and_11 (and_11_out, not_20_out, A, B);
  not not_21 (not_21_out, A);
  and and_12 (and_12_out, L, not_21_out, not_22_out);
  not not_22 (not_22_out, B);
  not not_23 (not_23_out, L);
  and and_13 (and_13_out, not_23_out, A, B);
  not not_24 (not_24_out, A);
  and and_14 (and_14_out, L, not_24_out, not_25_out);
  not not_25 (not_25_out, B);
  not not_26 (not_26_out, L);
  and and_15 (and_15_out, not_26_out, A, not_27_out);
  not not_27 (not_27_out, C);
  not not_28 (not_28_out, L);
  and and_16 (and_16_out, not_28_out, A, B);
  and and_17 (and_17_out, L, not_29_out, not_30_out);
  not not_29 (not_29_out, A);
  not not_30 (not_30_out, B);
  and and_18 (and_18_out, L, not_31_out, C);
  not not_31 (not_31_out, A);
  not not_32 (not_32_out, L);
  and and_19 (and_19_out, not_32_out, C);
  not not_33 (not_33_out, L);
  and and_20 (and_20_out, not_33_out, A, B);
  and and_21 (and_21_out, L, not_34_out, not_35_out);
  not not_34 (not_34_out, A);
  not not_35 (not_35_out, B);
  and and_22 (and_22_out, L, not_36_out);
  not not_36 (not_36_out, C);
  and and_23 (and_23_out, not_1_out, A, B, not_2_out);
  or or_1 (Fa, and_23_out, and_24_out);
  and and_24 (and_24_out, L, not_3_out, not_4_out, C);
  or or_2 (Fb, and_1_out, and_2_out, and_3_out, and_4_out);
  or or_3 (Fd, and_11_out, and_12_out);
  or or_4 (Fe, and_13_out, and_14_out);
  or or_5 (Ff, and_15_out, and_16_out, and_17_out, and_18_out);
  or or_6 (Fg, and_19_out, and_20_out, and_21_out, and_22_out);
  or or_7 (Fc, and_5_out, and_6_out, and_7_out, and_8_out, and_9_out, and_10_out);
endmodule
