// Logisim project ECE02017.circ as structural Verilog: 2 circuits, main circuit main
module main (
  input  L,
  input  RESET
);

  wire clock_1_out, text_out_1_a_2, text_out_1_b_2, text_out_1_c_2, text_out_1_d, text_out_1_e, text_out_1_f,
       text_out_1_g;
  wire [3:0] counter_1_q;

  Clock clock_1 (.out(clock_1_out));
  Counter #(.width(4), .max('h7)) counter_1 (
    .load(L), .Q(counter_1_q), .clk(clock_1_out), .clr(RESET));  // open: D, count, carry
  TEXT_OUT text_out_1 (
    .A(counter_1_q[2]), .B(counter_1_q[1]), .C(counter_1_q[0]), .a_2(text_out_1_a_2), .b_2(text_out_1_b_2),
    .c_2(text_out_1_c_2), .d(text_out_1_d), .e(text_out_1_e), .f(text_out_1_f), .g(text_out_1_g));
  _7_Segment_Display #(.active("false")) u_7_segment_display_1 (
    .g(text_out_1_g), .f(text_out_1_f), .a(text_out_1_a_2), .b(text_out_1_b_2), .e(text_out_1_e),
    .d(text_out_1_d), .c(text_out_1_c_2), .dp(1'b1));

  // Notes on the sheet:
  //   CLOCK
  //   7493
  //   ATF20GV8
endmodule

module TEXT_OUT (
  input  A,
  input  B,
  input  C,
  output a_2,
  output b_2,
  output c_2,
  output d,
  output e,
  output f,
  output g
);

  wire and_3_out, and_5_out, and_6_out, and_7_out, and_8_out, and_9_out, and_10_out, and_11_out, not_1_out,
       not_2_out, not_3_out, not_4_out, not_5_out, not_6_out, not_7_out, not_8_out, not_9_out, not_10_out,
       not_11_out, not_12_out;

  not not_1 (not_1_out, C);
  not not_2 (not_2_out, A);
  not not_3 (not_3_out, B);
  not not_4 (not_4_out, A);
  not not_5 (not_5_out, C);
  not not_6 (not_6_out, A);
  not not_7 (not_7_out, B);
  not not_8 (not_8_out, A);
  not not_9 (not_9_out, C);
  not not_10 (not_10_out, B);
  not not_11 (not_11_out, C);
  and and_1 (d, A, B);
  and and_2 (e, A, B);
  not not_12 (not_12_out, C);
  and and_3 (and_3_out, A, B);
  and and_4 (a_2, A, B, not_1_out);
  and and_5 (and_5_out, not_2_out, not_3_out);
  and and_6 (and_6_out, not_4_out, not_5_out);
  and and_7 (and_7_out, not_6_out, not_7_out);
  and and_8 (and_8_out, not_8_out, not_9_out);
  and and_9 (and_9_out, not_10_out, not_11_out);
  and and_10 (and_10_out, A, not_12_out);
  and and_11 (and_11_out, A, B);
  or or_1 (g, C, and_3_out);
  or or_2 (b_2, and_5_out, and_6_out);
  or or_3 (c_2, and_7_out, and_8_out, and_9_out);
  or or_4 (f, and_10_out, and_11_out);
endmodule
