// Logisim project Εργασήριο1-Β-604-2017.circ as structural Verilog: 3 circuits, main circuit main
module main (
  input  A,
  input  B,
  input  C,
  output F2
);

  wire U1A_out, U1B_out, U1C_out, U2A_out, U2B_out, U2C_out;

  not U1A (U1A_out, A);
  not U1B (U1B_out, B);
  not U1C (U1C_out, C);
  and U2A (U2A_out, U1A_out, B, C);
  and U2B (U2B_out, U1B_out, A, C);
  and U2C (U2C_out, U1C_out, B, A);
  or U3 (F2, U2A_out, U2B_out, U2C_out);

  // Notes on the sheet:
  //   A'BC
  //   AB'C
  //   ABC'
endmodule

module TEST2 (
  input  A,
  input  B,
  input  C,
  output F2
);

  wire and_1_out, and_2_out, and_3_out, and_4_out, and_5_out, and_6_out, not_1_out, not_2_out, not_3_out,
       or_1_out;

  not not_1 (not_1_out, A);
  not not_2 (not_2_out, B);
  and and_1 (and_1_out, not_1_out, B);
  and and_2 (and_2_out, A, not_2_out);
  and and_3 (and_3_out, and_1_out, C);
  and and_4 (and_4_out, and_2_out, C);
  and and_5 (and_5_out, A, B);
  not not_3 (not_3_out, C);
  or or_1 (or_1_out, and_3_out, and_4_out);
  and and_6 (and_6_out, and_5_out, not_3_out);
  or or_2 (F2, or_1_out, and_6_out);

  // Notes on the sheet:
  //   A'B
  //   (A'B)C
endmodule

module TEST3 (
  input  A,
  input  B,
  input  C,
  output F2
);

  wire nand_1_out, nand_2_out, nand_3_out, nand_4_out, nand_5_out, nand_6_out;

  nand nand_1 (nand_1_out, A, A);
  nand nand_2 (nand_2_out, B, B);
  nand nand_3 (nand_3_out, C, C);
  nand nand_4 (nand_4_out, nand_1_out, B, C);
  nand nand_5 (nand_5_out, A, nand_2_out, C);
  nand nand_6 (nand_6_out, A, B, nand_3_out);
  nand nand_7 (F2, nand_4_out, nand_5_out, nand_6_out);
endmodule
