// Logisim project Εργαστήριο1-C-604-2017.circ as structural Verilog
module TEST4 (
  input  A,
  input  B,
  input  C,
  input  D,
  output F3
);

  wire and_1_out, and_2_out, and_3_out, and_4_out, and_5_out, and_6_out;

  and and_1 (and_1_out, C, D);
  and and_2 (and_2_out, B, D);
  and and_3 (and_3_out, B, C);
  and and_4 (and_4_out, A, D);
  and and_5 (and_5_out, A, C);
  and and_6 (and_6_out, A, B);
  or or_1 (F3, and_1_out, and_2_out, and_3_out, and_4_out, and_5_out, and_6_out);
endmodule

module TEST5 (
  input  A,
  input  B,
  input  C,
  input  D,
  output F3
);

  wire and_1_out, and_2_out, and_3_out, and_4_out, and_5_out, and_6_out, or_1_out, or_2_out, or_3_out,
       or_4_out;

  and and_1 (and_1_out, C, D);
  and and_2 (and_2_out, B, D);
  and and_3 (and_3_out, A, D);
  and and_4 (and_4_out, A, C);
  or or_1 (or_1_out, and_1_out, and_2_out);
  or or_2 (or_2_out, or_1_out, and_5_out);
  and and_5 (and_5_out, B, C);
  or or_3 (or_3_out, and_3_out, and_4_out);
  or or_4 (or_4_out, or_3_out, and_6_out);
  and and_6 (and_6_out, A, B);
  or or_5 (F3, or_2_out, or_4_out);
endmodule

module TEST6 (
  input  A,
  input  B,
  input  C,
  input  D,
  output F3
);

  wire nand_1_out, nand_2_out, nand_3_out, nand_4_out, nand_5_out, nand_6_out;

  nand nand_1 (nand_1_out, C, D);
  nand nand_2 (nand_2_out, B, D);
  nand nand_3 (nand_3_out, B, C);
  nand nand_4 (nand_4_out, A, D);
  nand nand_5 (nand_5_out, A, C);
  nand nand_6 (nand_6_out, A, B);
  nand nand_7 (F3, nand_1_out, nand_2_out, nand_3_out, nand_4_out, nand_5_out, nand_6_out);
endmodule
