// Logisim project Εργαστήριο1-Α-604-2017.circ as structural Verilog: 2 circuits, main circuit main
module main (
  input  A,
  input  B,
  output F1
);

  wire U1A_out, U1B_out, U2A_out, U2B_out;

  not U2A (U2A_out, A);
  not U2B (U2B_out, B);
  and U1A (U1A_out, U2A_out, B);
  and U1B (U1B_out, A, U2B_out);
  or U3A (F1, U1A_out, U1B_out);
endmodule

module TEST1 (
  input  A,
  input  B,
  output F1
);

  wire and_1_out, and_2_out, not_1_out, not_2_out;

  not not_1 (not_1_out, A);
  not not_2 (not_2_out, B);
  and and_1 (and_1_out, not_1_out, B);
  and and_2 (and_2_out, A, not_2_out);
  or or_1 (F1, and_1_out, and_2_out);
endmodule
