// Logisim project ERGASTHRIO_2.circ as structural Verilog: 2 circuits, main circuit main
module main (
  input  A,
  input  B
);

  wire display_1_fa, display_1_fb, display_1_fc, display_1_fd, display_1_fe, display_1_ff, display_1_fg,
       display_1_fh;

  DISPLAY display_1 (
    .A(A), .B(B), .FA(display_1_fa), .FB(display_1_fb), .FC(display_1_fc), .FD(display_1_fd),
    .FE(display_1_fe), .FF(display_1_ff), .FG(display_1_fg), .FH(display_1_fh));
  _7_Segment_Display #(.active("false")) u_7_segment_display_1 (
    .g(display_1_fg), .f(display_1_ff), .a(display_1_fa), .b(display_1_fb), .e(display_1_fe),
    .d(display_1_fd), .c(display_1_fc), .dp(display_1_fh));

  // Notes on the sheet:
  //   FA
  //   FB
  //   FC
  //   FD
  //   FE
  //   FF
  //   FG
  //   FH
endmodule

module DISPLAY (
  input  A,
  input  B,
  output FA,
  output FB,
  output FC,
  output FD,
  output FE,
  output FF,
  output FG,
  output FH
);

  wire not_1_out, not_2_out, not_3_out;

  not not_1 (not_1_out, A);
  not not_2 (not_2_out, B);
  not not_3 (not_3_out, A);
  or or_1 (FF, B, A);
  not not_4 (FG, A);
  and and_1 (FA, not_1_out, B);
  and and_2 (FC, A, not_2_out);
  and and_3 (FD, not_3_out, B);

  assign FB = 1'b0;
  assign FE = B;
  assign FH = 1'b1;
endmodule
