// Logisim project LAB-EXERCISE3----604-2017.circ as structural Verilog: 1 circuit, main circuit main
module main (
  input  A,
  input  B,
  input  C,
  output _11,
  output _3
);

  wire U1_out, U3_out;

  or U3 (U3_out, A, B);
  not U1 (U1_out, C);
  or U3_2 (_11, U3_out, U1_out);
  and U2 (_3, U1_out, U3_out);

  // Notes on the sheet:
  //   1
  //   2
  //   1
  //   3
  //   2
  //   13
  //   12
  //   1
  //   2
endmodule
