// Logisim project LAB-EXERCISE5--ILIAS-STATHAKOS--2017.circ as structural Verilog: 2 circuits, main circuit main
module main (
  input  Cin,
  input  \Α0 ,
  input  \Β0 ,
  input  \Α1 ,
  input  \Β1 ,
  input  \Α2 ,
  input  \Β2 ,
  output S0,
  output S1,
  output S2,
  output S3
);

  wire adder_1_cout, adder_2_cout;

  adder adder_1 (.A(Cin), .B(\Α0 ), .Cin(\Β0 ), .S(S0), .Cout(adder_1_cout));
  adder adder_2 (.A(adder_1_cout), .B(\Α1 ), .Cin(\Β1 ), .S(S1), .Cout(adder_2_cout));
  adder adder_3 (.A(adder_2_cout), .B(\Α2 ), .Cin(\Β2 ), .S(S2), .Cout(S3));

  // Notes on the sheet:
  //   Cout0
  //   Cout1
  //   Cout2
endmodule

// ADD
module adder (
  input  A,
  input  B,
  input  Cin,
  output S,
  output Cout
);

  wire and_1_out, and_2_out, and_3_out;

  xor xor_1 (S, A, B, Cin);
  and and_1 (and_1_out, B, Cin);
  and and_2 (and_2_out, A, B);
  and and_3 (and_3_out, A, Cin);
  or or_1 (Cout, and_1_out, and_2_out, and_3_out);
endmodule
