// Logisim project BCD--2017.circ as structural Verilog: 2 circuits, main circuit main
module main (
  input  C4,
  input  S3,
  input  S2,
  input  S1,
  input  S0
);

  wire bcd_2017_1_a, bcd_2017_1_b, bcd_2017_1_c, bcd_2017_1_d, bcd_2017_1_e, bcd_2017_1_f, bcd_2017_1_g,
       bcd_2017_1_h;

  BCD_2017 bcd_2017_1 (
    .C4(C4), .S3(S3), .S2(S2), .S1(S1), .S0(S0), .A(bcd_2017_1_a), .B(bcd_2017_1_b), .C(bcd_2017_1_c),
    .D(bcd_2017_1_d), .E(bcd_2017_1_e), .F(bcd_2017_1_f), .G(bcd_2017_1_g), .H(bcd_2017_1_h));
  _7_Segment_Display #(.active("false")) u_7_segment_display_1 (
    .g(bcd_2017_1_g), .f(bcd_2017_1_f), .a(bcd_2017_1_a), .b(bcd_2017_1_b), .e(bcd_2017_1_e),
    .d(bcd_2017_1_d), .c(bcd_2017_1_c), .dp(bcd_2017_1_h));
endmodule

module BCD_2017 (
  input  C4,
  input  S3,
  input  S2,
  input  S1,
  input  S0,
  output A,
  output B,
  output C,
  output D,
  output E,
  output F,
  output G,
  output H
);

  wire and_1_out, and_2_out, and_3_out, and_4_out, and_5_out, and_6_out, and_7_out, and_8_out, and_9_out,
       and_10_out, and_11_out, and_12_out, and_13_out, and_14_out, and_15_out, and_16_out, and_17_out,
       and_18_out, and_19_out, and_20_out, and_21_out, and_22_out, and_23_out, and_24_out, and_25_out,
       and_26_out, and_27_out, and_28_out, not_1_out, not_2_out, not_3_out, not_4_out, not_5_out, not_6_out,
       not_7_out, not_8_out, not_9_out, not_10_out, not_11_out, not_12_out, not_13_out, not_14_out,
       not_15_out, not_16_out, not_17_out, not_18_out, not_19_out, not_20_out, not_21_out, not_22_out,
       not_23_out, not_24_out, not_25_out, not_26_out, not_27_out, not_28_out, not_29_out, not_30_out,
       not_31_out, not_32_out, not_33_out, not_34_out, not_35_out, not_36_out, not_37_out, not_38_out,
       not_39_out, not_40_out, not_41_out, not_42_out, not_43_out, not_44_out, not_45_out, not_46_out,
       not_47_out, not_48_out, not_49_out, not_50_out;

  not not_1 (not_1_out, C4);
  not not_2 (not_2_out, S3);
  not not_3 (not_3_out, S2);
  not not_4 (not_4_out, S1);
  not not_5 (not_5_out, S3);
  not not_6 (not_6_out, S1);
  not not_7 (not_7_out, S0);
  not not_8 (not_8_out, S2);
  not not_9 (not_9_out, S0);
  not not_10 (not_10_out, S3);
  not not_11 (not_11_out, S1);
  not not_12 (not_12_out, S3);
  not not_13 (not_13_out, S0);
  not not_14 (not_14_out, S1);
  not not_15 (not_15_out, S0);
  not not_16 (not_16_out, C4);
  not not_17 (not_17_out, S3);
  not not_18 (not_18_out, S2);
  not not_19 (not_19_out, S0);
  not not_20 (not_20_out, S1);
  not not_21 (not_21_out, S0);
  not not_22 (not_22_out, S2);
  not not_23 (not_23_out, S1);
  not not_24 (not_24_out, S3);
  not not_25 (not_25_out, S1);
  not not_26 (not_26_out, S0);
  not not_27 (not_27_out, S3);
  not not_28 (not_28_out, S2);
  not not_29 (not_29_out, S0);
  not not_30 (not_30_out, S3);
  not not_31 (not_31_out, S1);
  not not_32 (not_32_out, S3);
  not not_33 (not_33_out, S2);
  not not_34 (not_34_out, C4);
  not not_35 (not_35_out, S3);
  not not_36 (not_36_out, S2);
  not not_37 (not_37_out, S3);
  not not_38 (not_38_out, S2);
  not not_39 (not_39_out, S1);
  not not_40 (not_40_out, C4);
  not not_41 (not_41_out, S3);
  not not_42 (not_42_out, S2);
  not not_43 (not_43_out, S1);
  not not_44 (not_44_out, S3);
  not not_45 (not_45_out, S2);
  not not_46 (not_46_out, C4);
  not not_47 (not_47_out, S3);
  not not_48 (not_48_out, C4);
  not not_49 (not_49_out, S2);
  not not_50 (not_50_out, S1);
  and and_1 (and_1_out, not_1_out, not_2_out, not_3_out, not_4_out, S0);
  and and_2 (and_2_out, not_5_out, S2, not_6_out, not_7_out);
  and and_3 (and_3_out, S3, not_8_out, S1, S0);
  and and_4 (and_4_out, S3, S2, S1, not_9_out);
  and and_5 (and_5_out, not_10_out, S2, not_11_out, S0);
  and and_6 (and_6_out, not_12_out, S2, S1, not_13_out);
  and and_7 (and_7_out, S3, S2, S1, S0);
  and and_8 (and_8_out, C4, not_14_out, not_15_out);
  and and_9 (and_9_out, not_16_out, not_17_out, not_18_out, S1, not_19_out);
  and and_10 (and_10_out, S3, S2, not_20_out, not_21_out);
  and and_11 (and_11_out, not_22_out, not_23_out, S0);
  and and_12 (and_12_out, not_24_out, S2, not_25_out, not_26_out);
  and and_13 (and_13_out, not_27_out, S2, S1, S0);
  and and_14 (and_14_out, S3, not_28_out, S0);
  and and_15 (and_15_out, S3, S2, S1, not_29_out);
  and and_16 (and_16_out, not_30_out, S2, not_31_out);
  and and_17 (and_17_out, S3, S2, S1);
  and and_18 (and_18_out, not_32_out, not_33_out, S0);
  and and_19 (and_19_out, not_34_out, not_35_out, not_36_out, S1);
  and and_20 (and_20_out, not_37_out, S1, S0);
  and and_21 (and_21_out, not_38_out, S1, S0);
  and and_22 (and_22_out, S3, S2, not_39_out);
  and and_23 (and_23_out, not_40_out, not_41_out, not_42_out, not_43_out);
  and and_24 (and_24_out, not_44_out, S2, S1, S0);
  and and_25 (and_25_out, S3, not_45_out, S1);
  and and_26 (and_26_out, C4, S0);
  and and_27 (and_27_out, not_46_out, not_47_out);
  and and_28 (and_28_out, not_48_out, not_49_out, not_50_out);
  or or_1 (A, and_1_out, and_2_out, and_3_out, and_4_out);
  or or_2 (B, and_5_out, and_6_out, and_7_out, and_8_out);
  or or_3 (C, and_9_out, and_10_out);
  or or_4 (D, and_11_out, and_12_out, and_13_out, and_14_out, and_15_out);
  or or_5 (E, S0, and_16_out, and_17_out);
  or or_6 (F, and_18_out, and_19_out, and_20_out, and_21_out, and_22_out);
  or or_7 (G, and_23_out, and_24_out, and_25_out, and_26_out);
  or or_8 (H, and_27_out, and_28_out);
endmodule
