// Logisim project ERGASTHRIO_8.circ as structural Verilog: 3 circuits, main circuit main
module main (
  input  in_1,
  output [3:0] out_2
);

  wire clock_1_out, text_out_1_a_2, text_out_1_b_2, text_out_1_c_2, text_out_1_d, text_out_1_e, text_out_1_f,
       text_out_1_g, text_out_1_h;
  wire [2:0] state_1_d0;

  STATE state_1 (
    .X(in_1), .Q2(out_2[2]), .Q1(out_2[1]), .Q0(out_2[0]), .D2(state_1_d0[2]), .D1(state_1_d0[1]),
    .D0(state_1_d0[0]));
  Clock clock_1 (.out(clock_1_out));
  Register #(.width(4)) register_1 (.D({1'b0, state_1_d0}), .Q(out_2), .clk(clock_1_out));  // open: en, clr
  TEXT_OUT text_out_1 (
    .A(out_2[2]), .B(out_2[1]), .C(out_2[0]), .a_2(text_out_1_a_2), .b_2(text_out_1_b_2),
    .c_2(text_out_1_c_2), .d(text_out_1_d), .e(text_out_1_e), .f(text_out_1_f), .g(text_out_1_g),
    .h(text_out_1_h));
  _7_Segment_Display #(.active("false")) u_7_segment_display_1 (
    .g(text_out_1_g), .f(text_out_1_f), .a(text_out_1_a_2), .b(text_out_1_b_2), .e(text_out_1_e),
    .d(text_out_1_d), .c(text_out_1_c_2), .dp(text_out_1_h));

  // Notes on the sheet:
  //   ATF20GV8
  //   ΑΚΟΛΟΥΘΙΑΚΟ ΚΥΚΛΩΜΑ
  //   74194
  //   ATF20GV8
  //   ΣΥΝΔΙΑΣΤΙΚΟ ΚΥΚΛΩΜΑ
endmodule

module TEXT_OUT (
  input  A,
  input  B,
  input  C,
  output a_2,
  output b_2,
  output c_2,
  output d,
  output e,
  output f,
  output g,
  output h
);

  wire and_1_out, and_2_out, and_5_out, and_6_out, and_7_out, and_8_out, and_9_out, and_10_out, and_11_out,
       and_12_out, and_13_out, and_14_out, and_15_out, not_1_out, not_2_out, not_3_out, not_4_out, not_5_out,
       not_6_out, not_7_out, not_8_out, not_9_out, not_10_out, not_11_out, not_12_out, not_13_out,
       not_14_out, not_15_out, not_16_out;

  not not_1 (not_1_out, A);
  not not_2 (not_2_out, C);
  not not_3 (not_3_out, B);
  not not_4 (not_4_out, A);
  not not_5 (not_5_out, C);
  not not_6 (not_6_out, A);
  not not_7 (not_7_out, A);
  not not_8 (not_8_out, B);
  not not_9 (not_9_out, C);
  not not_10 (not_10_out, B);
  not not_11 (not_11_out, C);
  not not_12 (not_12_out, B);
  not not_13 (not_13_out, A);
  not not_14 (not_14_out, C);
  not not_15 (not_15_out, B);
  not not_16 (not_16_out, C);
  and and_1 (and_1_out, not_1_out, not_2_out);
  and and_2 (and_2_out, not_3_out, C);
  and and_3 (b_2, not_4_out, B, not_5_out);
  and and_4 (c_2, not_6_out, B);
  and and_5 (and_5_out, not_7_out, not_8_out);
  and and_6 (and_6_out, B, not_9_out);
  and and_7 (and_7_out, A, C);
  and and_8 (and_8_out, not_10_out, C);
  and and_9 (and_9_out, B, not_11_out);
  and and_10 (and_10_out, A, B);
  and and_11 (and_11_out, not_12_out, C);
  and and_12 (and_12_out, not_13_out, B);
  and and_13 (and_13_out, B, not_14_out);
  and and_14 (and_14_out, not_15_out, C);
  and and_15 (and_15_out, A, not_16_out);
  or or_1 (a_2, and_1_out, and_2_out);
  or or_2 (d, and_5_out, and_6_out, and_7_out);
  or or_3 (e, and_8_out, and_9_out, and_10_out);
  or or_4 (f, and_11_out, and_12_out, and_13_out);
  or or_5 (g, and_14_out, and_15_out);

  assign h = 1'b1;
endmodule

module STATE (
  input  X,
  input  Q2,
  input  Q1,
  input  Q0,
  output D2,
  output D1,
  output D0
);

  wire and_1_out, and_2_out, and_3_out, and_4_out, and_5_out, and_6_out, and_7_out, and_8_out, and_9_out,
       and_10_out, and_11_out, and_12_out, and_13_out, and_14_out, not_1_out, not_2_out, not_3_out,
       not_4_out, not_5_out, not_6_out, not_7_out, not_8_out, not_9_out, not_10_out, not_11_out, not_12_out,
       not_13_out, not_14_out, not_15_out, not_16_out, not_17_out, not_18_out, not_19_out, not_20_out;

  not not_1 (not_1_out, X);
  not not_2 (not_2_out, X);
  not not_3 (not_3_out, Q1);
  not not_4 (not_4_out, Q2);
  not not_5 (not_5_out, Q1);
  not not_6 (not_6_out, Q0);
  not not_7 (not_7_out, X);
  not not_8 (not_8_out, Q1);
  not not_9 (not_9_out, X);
  not not_10 (not_10_out, Q2);
  not not_11 (not_11_out, Q0);
  not not_12 (not_12_out, X);
  not not_13 (not_13_out, Q1);
  not not_14 (not_14_out, Q0);
  not not_15 (not_15_out, X);
  not not_16 (not_16_out, Q2);
  and and_1 (and_1_out, not_15_out, not_16_out, not_17_out);
  not not_17 (not_17_out, Q0);
  not not_18 (not_18_out, Q1);
  and and_2 (and_2_out, Q2, not_18_out, not_19_out);
  not not_19 (not_19_out, Q0);
  and and_3 (and_3_out, Q2, Q1, Q0);
  and and_4 (and_4_out, X, Q1, not_20_out);
  not not_20 (not_20_out, Q0);
  and and_5 (and_5_out, not_1_out, Q1, Q0);
  and and_6 (and_6_out, not_2_out, Q2, not_3_out);
  and and_7 (and_7_out, Q2, Q0);
  and and_8 (and_8_out, X, not_4_out, not_5_out, not_6_out);
  and and_9 (and_9_out, X, Q2, Q1);
  and and_10 (and_10_out, not_7_out, not_8_out, Q0);
  and and_11 (and_11_out, not_9_out, not_10_out, Q1, not_11_out);
  and and_12 (and_12_out, not_12_out, Q2, Q0);
  and and_13 (and_13_out, X, not_13_out, not_14_out);
  and and_14 (and_14_out, X, Q1, Q0);
  or or_1 (D0, and_1_out, and_2_out, and_3_out, and_4_out);
  or or_2 (D2, and_5_out, and_6_out, and_7_out, and_8_out, and_9_out);
  or or_3 (D1, and_10_out, and_11_out, and_12_out, and_13_out, and_14_out);
endmodule
